# Fritzing sketch fechaduraSketch (saved by Fritzing 1.0.6)
breadboards: 2

parts:
  Componente1 = Arduino Uno (Rev3) - ICSP
  SW1 = DIP Switch 8 Position [package=dipswitch-08]
  U1 = POT [knob_status=50% power=0.5W package=alps_pot]
  Grove1 = Grove OLED 128x96
  M1 = Dagu DGServo 9g (Pan and tilt) [part_number=RS001B]

nets:
  N1: Componente1.A0, U1.S
  VCC: Componente1.5V, SW1.9, SW1.10, SW1.11, SW1.12, SW1.13, U1.A, Grove1.VCC, M1.vcc
  N2: Componente1.A4/SDA, Grove1.SDA
  N3: Componente1.A5/SCL, Grove1.SCL
  N4: Componente1.D2, SW1.8
  N5: Componente1.D3_PWM, SW1.7
  N6: Componente1.D4, SW1.6
  N7: Componente1.D5_PWM, SW1.5
  N8: Componente1.D6_PWM, SW1.4
  N9: Componente1.D7, M1.pulse
  GND: Componente1.GND, U1.E, Grove1.GND, M1.gnd
